# Fritzing sketch schema-arduino-fritzing (saved by Fritzing 0.9.2b)

parts:
  Part1 = Arduino Mega 2560 (Rev3)
  Part2 = Arduino Ethernet Shield (Rev3)
  LCD1 = LCD screen
  DHT1 = DHT22 Humidity and Temperature Sensor
  R1 = Resistor [tolerance=±5% resistance=220 package=THT]
  R2 = Rotary Potentiometer (Large) [maximum_resistance=100kΩ package=THT]
  S1 = Pushbutton [package="[THT]"]
  S2 = Pushbutton [package="[THT]"]
  S3 = Pushbutton [package="[THT]"]
  S4 = Pushbutton [package="[THT]"]
  S5 = Pushbutton [package="[THT]"]
  S6 = Pushbutton [package="[THT]"]
  R3 = Resistor [tolerance=±5% resistance=10k package=THT]
  R4 = Resistor [tolerance=±5% resistance=10k package=THT]
  R5 = Resistor [tolerance=±5% resistance=10k package=THT]
  R6 = Resistor [tolerance=±5% resistance=10k package=THT]
  R7 = Resistor [tolerance=±5% resistance=10k package=THT]
  R8 = Resistor [tolerance=±5% resistance=10k package=THT]

nets:
  5V: Part1.5V, LCD1.VDD, LCD1.LED+, R2.leg1
  N1: Part1.D23, LCD1.RS
  N2: Part1.D25, LCD1.E
  N3: Part1.D27, LCD1.DB4
  N4: Part1.D29, LCD1.DB5
  N5: Part1.D31, LCD1.DB6
  N6: Part1.D33, LCD1.DB7
  N7: Part1.D41, S6.Pin_1, S6.Pin_2, R8.Pin_0
  N8: Part1.D43, S5.Pin_1, S5.Pin_2, R7.Pin_0
  N9: Part1.D45, S4.Pin_1, S4.Pin_2, R6.Pin_0
  N10: Part1.D47, S3.Pin_1, S3.Pin_2, R5.Pin_0
  N11: Part1.D49, S2.Pin_1, S2.Pin_2, R4.Pin_0
  N12: Part1.D51, S1.Pin_1, S1.Pin_2, R3.Pin_0
  N13: Part1.D53, DHT1.DATA, R1.Pin_0
  GND: Part1.GND, LCD1.VSS, LCD1.R/W, LCD1.LED-, R2.leg2
  5V_2: Part2.5V, DHT1.VDD, R1.Pin_1, S1.Pin_4, S2.Pin_4, S3.Pin_3, S3.Pin_4, S4.Pin_3, S4.Pin_4, S5.Pin_4, S6.Pin_4
  GND_2: Part2.GND, DHT1.GND, R3.Pin_1, R4.Pin_1, R5.Pin_1, R6.Pin_1, R7.Pin_1, R8.Pin_1
  N14: LCD1.V0, R2.wiper

notes:
  Pins 10, 11, 12, 13 on the Arduino Ethernet Shield are used, do not use them + The SD card takes pin 4 on the Arduino Ethernet Shield
  Relay to control the light
  Button 1:
  - Menu to change target temperature
  - Decrement value
  Button 2:
  - Change light mode (AUTO, ON, OFF)
  - Increment value
  Button 3:
  - ???
  - Ok
  Button 4:
  - ???
  Button 5:
  - ???
  Button 6:
  - ???
  < Button 1
  Button 6 >
